# Fritzing sketch SimonTiltLight (saved by Fritzing 0.9.3b)
breadboards: 1

parts:
  LED1 = smd LED [color="Red (633nm)" package="0603 [SMD]"]
  LED2 = smd LED [color="Green (570nm)" package="0603 [SMD]"]
  LED3 = smd LED [color="Yellow (595nm)" package="0603 [SMD]"]
  LED4 = smd LED [color="Orange (620nm)" package="0603 [SMD]"]
  LED5 = smd LED [color="Blue (525nm)" package="0603 [SMD]"]
  LED6 = smd LED [color="White (4500K)" package="0603 [SMD]"]
  R1 = Resistor [tolerance=±5% resistance=220 package="0402 [SMD]"]
  R2 = Resistor [tolerance=±5% resistance=220 package="0402 [SMD]"]
  R3 = Resistor [tolerance=±5% resistance=220 package="0402 [SMD]"]
  R4 = Resistor [tolerance=±5% resistance=220 package="0402 [SMD]"]
  R5 = Resistor [tolerance=±5% resistance=220 package="0402 [SMD]"]
  R6 = Resistor [tolerance=±5% resistance=220 package="0402 [SMD]"]
  Part1 = Arduino Uno (Rev3)
  S1 = Momentary Switch [package=ksa_sealed_tac_switch]
  R7 = Resistor [tolerance=±5% resistance=10k package="0402 [SMD]"]
  Q2 = LTR-301 [package=ltr-301]
  Q3 = LTR-301 [package=ltr-301]
  Q4 = LTR-301 [package=ltr-301]
  Q5 = LTR-301 [package=ltr-301]
  Q6 = LTR-301 [package=ltr-301]
  R8 = Resistor [tolerance=±5% resistance=100k package="0402 [SMD]"]
  R9 = Resistor [tolerance=±5% resistance=100k package="0402 [SMD]"]
  R10 = Resistor [tolerance=±5% resistance=100k package="0402 [SMD]"]
  R11 = Resistor [tolerance=±5% resistance=100k package="0402 [SMD]"]
  R12 = Resistor [tolerance=±5% resistance=100k package="0402 [SMD]"]
  R13 = Resistor [tolerance=±5% resistance=100k package="0402 [SMD]"]
  Q1 = LTR-301 [package=ltr-301]
  U1 = Graphical LCD 128x64 [package=lcd-g12864]  # not connected

nets:
  N1: LED1.cathode, LED2.cathode, LED3.cathode, LED4.cathode, LED5.cathode, LED6.cathode, Part1.GND, R7.Pin_0, Q2.E, Q3.E, Q4.E, Q5.E, Q6.E, Q1.E
  N2: LED1.anode, R1.Pin_0
  N3: LED2.anode, R2.Pin_0
  N4: LED3.anode, R3.Pin_0
  N5: LED4.anode, R4.Pin_0
  N6: LED5.anode, R5.Pin_0
  N7: LED6.anode, R6.Pin_0
  N8: R1.Pin_1, Part1.D7
  N9: R2.Pin_1, Part1.D6_PWM
  N10: R3.Pin_1, Part1.D5_PWM
  N11: R4.Pin_1, Part1.D4
  N12: R5.Pin_1, Part1.D3_PWM
  N13: R6.Pin_1, Part1.D2
  N14: Part1.A0, R8.Pin_0, Q1.C
  N15: Part1.A1, Q2.C, R9.Pin_0
  N16: Part1.A2, Q3.C, R10.Pin_0
  N17: Part1.A3, Q4.C, R11.Pin_0
  N18: Part1.A4/SDA, Q5.C, R13.Pin_0
  N19: Part1.A5/SCL, Q6.C, R12.Pin_0
  N20: Part1.D8, S1.3, R7.Pin_1
  N21: Part1.5V, S1.1, R8.Pin_1, R9.Pin_1, R10.Pin_1, R11.Pin_1, R12.Pin_1, R13.Pin_1

// code stored in the sketch: SimonTiltLight.ino
const int greenLEDpin = 11;
const int redLEDpin   =  9;
const int blueLEDpin  = 10;

const int pin1 = 7;
const int pin2 = 6;
const int pin3 = 5;
const int pin4 = 4;
const int pin5 = 3;
const int pin6 = 2;

const int redSensorPin = A0;
const int greenSensorPin = A1;
const int blueSensorPin = A2;
const int photoSensorPin1 = A3;
const int photoSensorPin2 = A4;
const int photoSensorPin3 = A5;



int redValue = 0;
int greenValue = 0;
int blueValue =0;

int redSensorValue = 0;
int greenSensorValue = 0;
int blueSensorValue = 0;
int photoSensor1 = 0;
int photoSensor2 = 0;
int photoSensor3 = 0;

void setup() {
  Serial.begin(9600);

  pinMode(greenLEDpin, OUTPUT);
  pinMode(redLEDpin, OUTPUT);
  pinMode(blueLEDpin, OUTPUT);
  pinMode(pin1, OUTPUT);
  pinMode(pin2, OUTPUT);
  pinMode(pin3, OUTPUT);
  pinMode(pin4, OUTPUT);
  pinMode(pin5, OUTPUT);
  pinMode(pin6, OUTPUT);
  
}

void loop() {
  redSensorValue = analogRead(redSensorPin);
  delay(5);
  greenSensorValue = analogRead(greenSensorPin);
  delay(5);
  blueSensorValue = analogRead(blueSensorPin);
  delay(5);
  photoSensor1 = analogRead(photoSensorPin1);
  delay(5);
  photoSensor2 = analogRead(photoSensorPin2);
  delay(5);
  photoSensor3 = analogRead(photoSensorPin3);


  Serial.print("Raw Sensor Values \t Red: ");
  Serial.print(redSensorValue);
  Serial.print("\t Green: ");
  Serial.print(greenSensorValue);
  Serial.print("\t Blue: ");
  Serial.print(blueSensorValue);
  Serial.print("\t Photo Resistor 1: ");
  Serial.print(photoSensor1);
  Serial.print("\t Photo Resistor 2: ");
  Serial.print(photoSensor2);
  Serial.print("\t Photo Resistor 3: ");
  Serial.println(photoSensor3);

  

  redValue = redSensorValue/4;
  greenValue = greenSensorValue/4;
  blueValue = blueSensorValue/4;

  //Serial.print("Mapped Sensor Value \t Red: ");
  //Serial.print(redValue);
  //Serial.print("\t Green: ");
  //Serial.print(greenValue);
  //Serial.print("\t Blue: ");
  //Serial.println(blueValue);

  analogWrite(redLEDpin, redValue);
  analogWrite(greenLEDpin, greenValue);
  analogWrite(blueLEDpin, blueValue);

  if (redSensorValue < 3){ 
      Serial.println("PIN 1 LIT");
      digitalWrite(pin1, HIGH);
      digitalWrite(pin2, LOW);
      digitalWrite(pin3, LOW);
      digitalWrite(pin4, LOW);
      digitalWrite(pin5, LOW);
      digitalWrite(pin6, LOW);
      }
    else if (greenSensorValue < 3) {
      Serial.println("PIN 2 LIT");
      digitalWrite(pin1, LOW);
      digitalWrite(pin2, HIGH);
      digitalWrite(pin3, LOW);
      digitalWrite(pin4, LOW);
      digitalWrite(pin5, LOW);
      digitalWrite(pin6, LOW);
    }
    
     else if (blueSensorValue < 3) {
      Serial.println("PIN 3 LIT");
      digitalWrite(pin1, LOW);
      digitalWrite(pin2, LOW);
      digitalWrite(pin3, HIGH);
      digitalWrite(pin4, LOW);
      digitalWrite(pin5, LOW);
      digitalWrite(pin6, LOW);
    }

    else if (photoSensor1 < 3) {
      Serial.println("PIN 4 LIT");
      digitalWrite(pin1, LOW);
      digitalWrite(pin2, LOW);
      digitalWrite(pin3, LOW);
      digitalWrite(pin4, HIGH);
      digitalWrite(pin5, LOW);
      digitalWrite(pin6, LOW);
    }

    else if (photoSensor2 < 3) {
      Serial.println("PIN 5 LIT");
      digitalWrite(pin1, LOW);
      digitalWrite(pin2, LOW);
      digitalWrite(pin3, LOW);
      digitalWrite(pin4, LOW);
      digitalWrite(pin5, HIGH);
      digitalWrite(pin6, LOW);
    }

    else if (photoSensor3 < 3) {
      Serial.println("PIN 6 LIT");
      digitalWrite(pin1, LOW);
      digitalWrite(pin2, LOW);
      digitalWrite(pin3, LOW);
      digitalWrite(pin4, LOW);
      digitalWrite(pin5, LOW);
      digitalWrite(pin6, HIGH);
    }
    else{
      digitalWrite(pin1, LOW);
      digitalWrite(pin2, LOW);
      digitalWrite(pin3, LOW);
      digitalWrite(pin4, LOW);
      digitalWrite(pin5, LOW);
      digitalWrite(pin6, LOW);
    }
}
